// Logisim project logisim_project.circ as structural Verilog: 3 circuits, main circuit main
module main (
);

  wire [3:0] A_REG_q, ACU_q, B_REG_q, n4bit_alu_1_result, RAM_ADDR_q;
  wire [7:0] PROG_COUNTER_q;

  Register #(.width(4)) A_REG (.D(ACU_q), .Q(A_REG_q));  // open: en, clk, clr
  Register #(.width(4)) B_REG (.D(ACU_q), .Q(B_REG_q));  // open: en, clk, clr
  Counter PROG_COUNTER (.Q(PROG_COUNTER_q));  // open: load, D, count, carry, clk, clr
  _4bit_ALU u_4bit_alu_1 (.A(A_REG_q), .B(B_REG_q), .Result(n4bit_alu_1_result));  // open: Op
  Register #(.width(4)) ACU (.D(n4bit_alu_1_result), .Q(ACU_q));  // open: en, clk, clr
  ROM rom_1 (.addr(PROG_COUNTER_q));  // open: data, sel
  Register #(.width(4)) RAM_ADDR (.D(ACU_q), .Q(RAM_ADDR_q));  // open: en, clk, clr
  RAM #(.addrWidth(4), .dataWidth(4)) ram_1 (.addr(RAM_ADDR_q), .data(ACU_q));  // open: sel, clk, ld, clr
endmodule

module _1bit_ALU (
  input  Sub,
  input  Cin,
  input  [2:0] Sel,
  input  A,
  input  B,
  input  Less,
  output Result,
  output Cout,
  output Set
);

  wire and_1_out, nor_1_out, or_1_out, xor_1_out, xor_2_out;

  and and_1 (and_1_out, A, B);
  or or_1 (or_1_out, A, B);
  nor nor_1 (nor_1_out, A, B);
  xor xor_1 (xor_1_out, A, B);
  Adder #(.width(1)) adder_1 (.a(A), .b(xor_2_out), .out(Set), .cin(Cin), .cout(Cout));
  xor xor_2 (xor_2_out, B, Sub);
  Multiplexer #(.select(3), .enable("false")) multiplexer_1 (
    .in0(and_1_out), .in1(or_1_out), .in2(nor_1_out), .in3(xor_1_out), .in4(Set), .in5(Less), .in7(Set),
    .out(Result), .sel(Sel));  // open: in6
endmodule

module _4bit_ALU (
  input  [2:0] Op,
  input  [3:0] A,
  input  [3:0] B,
  output [3:0] Result
);

  wire and_1_out, n1bit_alu_1_cout, n1bit_alu_2_cout, n1bit_alu_3_cout, n1bit_alu_4_set;

  and and_1 (and_1_out, Op[0], Op[1], Op[2]);
  _1bit_ALU u_1bit_alu_1 (
    .A(A[0]), .B(B[0]), .Less(n1bit_alu_4_set), .Result(Result[0]), .Sub(and_1_out), .Cin(and_1_out),
    .Sel(Op), .Cout(n1bit_alu_1_cout));  // open: Set
  _1bit_ALU u_1bit_alu_2 (
    .A(A[1]), .B(B[1]), .Less(1'b0), .Result(Result[1]), .Sub(and_1_out), .Cin(n1bit_alu_1_cout), .Sel(Op),
    .Cout(n1bit_alu_2_cout));  // open: Set
  _1bit_ALU u_1bit_alu_3 (
    .A(A[2]), .B(B[2]), .Less(1'b0), .Result(Result[2]), .Sub(and_1_out), .Cin(n1bit_alu_2_cout), .Sel(Op),
    .Cout(n1bit_alu_3_cout));  // open: Set
  _1bit_ALU u_1bit_alu_4 (
    .A(A[3]), .B(B[3]), .Less(1'b0), .Result(Result[3]), .Sub(and_1_out), .Cin(n1bit_alu_3_cout), .Sel(Op),
    .Set(n1bit_alu_4_set));  // open: Cout
endmodule
